# Fritzing sketch RaspberryPI.SoftwareServo (saved by Fritzing 0.9.3b)
breadboards: 1

parts:
  Raspberry_Pi_1 = Raspberry Pi 3 [part_number=RPI-3-V1.2]
  J1 = Basic Servo

nets:
  3V3: Raspberry_Pi_1.3v3, J1.vcc
  N1: Raspberry_Pi_1.GPIO4, J1.pulse
  GND: Raspberry_Pi_1.GND, J1.gnd

notes:
  Yellow: Pin BCM #4 (Physical #7, wPi 09)
